// Logisim project 8bitadder.circ as structural Verilog: 7 circuits, main circuit Full adder
module Full_adder (
  input  x,
  input  y,
  input  C,
  output out_4,
  output out_5
);

  wire and_1_out, and_2_out, or_1_out;

  xor xor_1 (out_4, C, y, x);
  and and_1 (and_1_out, y, x);
  or or_1 (or_1_out, x, y);
  and and_2 (and_2_out, C, or_1_out);
  or or_2 (out_5, and_1_out, and_2_out);
endmodule

module Half_adder (
  input  a,
  input  b,
  output x,
  output y
);

  xor xor_1 (x, a, b);
  and and_1 (y, a, b);
endmodule

module _4_bit_adder (
  input  [3:0] in_1,
  input  [3:0] in_2,
  output [4:0] out_3
);

  wire full_adder_1_out_5, full_adder_2_out_5, full_adder_3_out_5;

  Full_adder full_adder_1 (.x(in_1[0]), .y(in_2[0]), .C(1'b0), .out_4(out_3[0]), .out_5(full_adder_1_out_5));
  Full_adder full_adder_2 (
    .x(in_1[2]), .y(in_2[2]), .C(full_adder_3_out_5), .out_4(out_3[2]), .out_5(full_adder_2_out_5));
  Full_adder full_adder_3 (
    .x(in_1[1]), .y(in_2[1]), .C(full_adder_1_out_5), .out_4(out_3[1]), .out_5(full_adder_3_out_5));
  Full_adder full_adder_4 (.x(in_1[3]), .y(in_2[3]), .C(full_adder_2_out_5), .out_4(out_3[3]), .out_5(out_3[4]));
endmodule

module _8_bit_adder (
  input  [7:0] in_1,
  input  [7:0] in_2,
  input  in_3,
  output [7:0] out_4,
  output out_5
);

  wire full_adder_2_1_u, full_adder_2_2_u, full_adder_2_3_u, full_adder_2_4_u, full_adder_2_5_u,
       full_adder_2_6_u, full_adder_2_7_u;

  Full_adder_2 full_adder_2_1 (.x(in_2[0]), .y(in_1[0]), .C(in_3), .z(out_4[0]), .u(full_adder_2_1_u));
  Full_adder_2 full_adder_2_2 (.x(in_2[1]), .y(in_1[1]), .C(full_adder_2_1_u), .z(out_4[1]), .u(full_adder_2_2_u));
  Full_adder_2 full_adder_2_3 (.x(in_2[2]), .y(in_1[2]), .C(full_adder_2_2_u), .z(out_4[2]), .u(full_adder_2_3_u));
  Full_adder_2 full_adder_2_4 (.x(in_2[3]), .y(in_1[3]), .C(full_adder_2_3_u), .z(out_4[3]), .u(full_adder_2_4_u));
  Full_adder_2 full_adder_2_5 (.x(in_2[4]), .y(in_1[4]), .C(full_adder_2_4_u), .z(out_4[4]), .u(full_adder_2_5_u));
  Full_adder_2 full_adder_2_6 (.x(in_2[5]), .y(in_1[5]), .C(full_adder_2_5_u), .z(out_4[5]), .u(full_adder_2_6_u));
  Full_adder_2 full_adder_2_7 (.x(in_2[6]), .y(in_1[6]), .C(full_adder_2_6_u), .z(out_4[6]), .u(full_adder_2_7_u));
  Full_adder_2 full_adder_2_8 (.x(in_2[7]), .y(in_1[7]), .C(full_adder_2_7_u), .z(out_4[7]), .u(out_5));
endmodule

module Full_adder_2 (
  input  x,
  input  y,
  input  C,
  output z,
  output u
);

  wire and_1_out, and_2_out, and_3_out, and_4_out, and_5_out, and_6_out, and_7_out, not_1_out, not_2_out,
       not_3_out, not_4_out, not_5_out, not_6_out;

  not not_1 (not_1_out, x);
  not not_2 (not_2_out, y);
  not not_3 (not_3_out, x);
  not not_4 (not_4_out, C);
  not not_5 (not_5_out, y);
  not not_6 (not_6_out, C);
  and and_1 (and_1_out, y, C);
  and and_2 (and_2_out, x, C);
  and and_3 (and_3_out, x, y);
  and and_4 (and_4_out, not_1_out, not_2_out, C);
  and and_5 (and_5_out, not_3_out, y, not_4_out);
  and and_6 (and_6_out, x, not_5_out, not_6_out);
  and and_7 (and_7_out, x, y, C);
  or or_1 (u, and_1_out, and_2_out, and_3_out);
  or or_2 (z, and_4_out, and_5_out, and_6_out, and_7_out);
endmodule

module _16_bit_adder_subtractor (
  input  in_1,
  input  [15:0] in_2,
  input  [15:0] in_3,
  output [15:0] out_4,
  output out_5
);

  wire n8_bit_adder_1_out_5, n8_bit_adder_2_out_5, not_1_out;
  wire [15:0] controlled_buffer_1_out;

  not not_1 (not_1_out, in_1);
  assign controlled_buffer_1_out = not_1_out ? in_2 : 16'bz;  // Controlled_Buffer controlled_buffer_1
  assign controlled_buffer_1_out = in_1 ? ~in_2 : 16'bz;  // Controlled_Inverter controlled_inverter_1
  _8_bit_adder u_8_bit_adder_1 (
    .in_1(controlled_buffer_1_out[7:0]), .in_2(in_3[7:0]), .out_4(out_4[7:0]), .in_3(in_1),
    .out_5(n8_bit_adder_1_out_5));
  _8_bit_adder u_8_bit_adder_2 (
    .in_1(controlled_buffer_1_out[15:8]), .in_2(in_3[15:8]), .out_4(out_4[15:8]),
    .in_3(n8_bit_adder_1_out_5), .out_5(n8_bit_adder_2_out_5));
  xor xor_1 (out_5, in_1, n8_bit_adder_2_out_5);
endmodule

module _8_bit_adder_subtractor (
  input  in_1,
  input  [7:0] in_2,
  input  [7:0] in_3,
  output [7:0] out_4,
  output out_5
);

  wire n8_bit_adder_1_out_5, not_1_out;
  wire [7:0] controlled_buffer_1_out;

  not not_1 (not_1_out, in_1);
  assign controlled_buffer_1_out = not_1_out ? in_2 : 8'bz;  // Controlled_Buffer controlled_buffer_1
  assign controlled_buffer_1_out = in_1 ? ~in_2 : 8'bz;  // Controlled_Inverter controlled_inverter_1
  _8_bit_adder u_8_bit_adder_1 (
    .in_1(controlled_buffer_1_out), .in_2(in_3), .out_4(out_4), .in_3(in_1), .out_5(n8_bit_adder_1_out_5));
  xor xor_1 (out_5, in_1, n8_bit_adder_1_out_5);
endmodule
