// Logisim project rszad1.circ as structural Verilog: 1 circuit, main circuit main
module main (
  input  [6:0] in_1,
  output [7:0] out_2
);

  wire and_1_out, and_2_out, and_3_out, and_4_out, decoder_1_out0, decoder_1_out1, decoder_1_out2,
       decoder_1_out3, decoder_1_out4, decoder_1_out5, decoder_1_out6, decoder_1_out7, not_1_out, or_1_out,
       or_2_out;

  not not_1 (not_1_out, in_1[3]);
  Decoder #(.select(3), .enable("false")) decoder_1 (
    .out0(decoder_1_out0), .out1(decoder_1_out1), .out2(decoder_1_out2), .out3(decoder_1_out3),
    .out4(decoder_1_out4), .out5(decoder_1_out5), .out6(decoder_1_out6), .out7(decoder_1_out7),
    .sel(in_1[6:4]));
  or or_1 (or_1_out, decoder_1_out7, decoder_1_out6);
  or or_2 (or_2_out, decoder_1_out5, decoder_1_out4);
  and and_1 (and_1_out, not_1_out, decoder_1_out0);
  and and_2 (and_2_out, in_1[3], decoder_1_out0);
  and and_3 (and_3_out, not_1_out, decoder_1_out1);
  and and_4 (and_4_out, in_1[3], decoder_1_out1);
  ROM #(.addrWidth(3), .dataWidth(4)) rom_1 (.addr(in_1[2:0]), .data(out_2[7:4]), .sel(and_1_out));
  ROM #(.addrWidth(3), .dataWidth(4)) rom_2 (.addr(in_1[2:0]), .data(out_2[7:4]), .sel(and_2_out));
  ROM #(.addrWidth(3), .dataWidth(4)) rom_3 (.addr(in_1[2:0]), .data(out_2[7:4]), .sel(and_3_out));
  ROM #(.addrWidth(3), .dataWidth(4)) rom_4 (.addr(in_1[2:0]), .data(out_2[7:4]), .sel(and_4_out));
  ROM #(.addrWidth(4), .dataWidth(4)) rom_5 (.addr(in_1[3:0]), .data(out_2[7:4]), .sel(decoder_1_out2));
  ROM #(.addrWidth(4), .dataWidth(4)) rom_6 (.addr(in_1[3:0]), .data(out_2[7:4]), .sel(decoder_1_out3));
  ROM #(.addrWidth(5), .dataWidth(4)) rom_7 (.addr(in_1[4:0]), .data(out_2[7:4]), .sel(or_2_out));
  ROM #(.addrWidth(5), .dataWidth(4)) rom_8 (.addr(in_1[4:0]), .data(out_2[7:4]), .sel(or_1_out));
  ROM #(.addrWidth(3), .dataWidth(4)) rom_9 (.addr(in_1[2:0]), .data(out_2[3:0]), .sel(and_1_out));
  ROM #(.addrWidth(3), .dataWidth(4)) rom_10 (.addr(in_1[2:0]), .data(out_2[3:0]), .sel(and_2_out));
  ROM #(.addrWidth(3), .dataWidth(4)) rom_11 (.addr(in_1[2:0]), .data(out_2[3:0]), .sel(and_3_out));
  ROM #(.addrWidth(3), .dataWidth(4)) rom_12 (.addr(in_1[2:0]), .data(out_2[3:0]), .sel(and_4_out));
  ROM #(.addrWidth(4), .dataWidth(4)) rom_13 (.addr(in_1[3:0]), .data(out_2[3:0]), .sel(decoder_1_out2));
  ROM #(.addrWidth(4), .dataWidth(4)) rom_14 (.addr(in_1[3:0]), .data(out_2[3:0]), .sel(decoder_1_out3));
  ROM #(.addrWidth(5), .dataWidth(4)) rom_15 (.addr(in_1[4:0]), .data(out_2[3:0]), .sel(or_2_out));
  ROM #(.addrWidth(5), .dataWidth(4)) rom_16 (.addr(in_1[4:0]), .data(out_2[3:0]), .sel(or_1_out));
endmodule
