// Logisim project 8bitComputer.circ as structural Verilog: 20 circuits, main circuit COMPUTER
module ALUblock (
  input  A,
  input  Ainv,
  input  B,
  input  Binv,
  input  Cin,
  output CONJUNCT,
  output DISJUNCT,
  output XDISJUNCT,
  output Cout,
  output SUM
);

  wire xor_1_out, xor_2_out;

  xor xor_1 (xor_1_out, A, Ainv);
  xor xor_2 (xor_2_out, B, Binv);
  Full_adder_8e202356 Full_adder_8e202356_1 (.out_5(Cout), .out_4(SUM), .C(Cin), .x(xor_2_out), .y(xor_1_out));
  and and_1 (CONJUNCT, xor_2_out, xor_1_out);
  or or_1 (DISJUNCT, xor_2_out, xor_1_out);
  xor xor_3 (XDISJUNCT, xor_2_out, xor_1_out);
endmodule

module COMPUTE (
  input  [7:0] A,
  input  [7:0] B,
  input  Ainv,
  input  Binv,
  input  Cin,
  output Cout,
  output [7:0] CONJUNCT,
  output [7:0] DISJUNCT,
  output [7:0] XDIJSJUNCT,
  output [7:0] SUM
);

  wire ALUblock_1_cout, ALUblock_2_cout, ALUblock_3_cout, ALUblock_4_cout, ALUblock_5_cout, ALUblock_6_cout,
       ALUblock_7_cout;

  ALUblock ALUblock_1 (
    .A(A[0]), .Ainv(Ainv), .B(B[0]), .Binv(Binv), .Cin(Cin), .CONJUNCT(CONJUNCT[0]), .DISJUNCT(DISJUNCT[0]),
    .XDISJUNCT(XDIJSJUNCT[0]), .Cout(ALUblock_1_cout), .SUM(SUM[0]));
  ALUblock ALUblock_2 (
    .A(A[1]), .Ainv(Ainv), .B(B[1]), .Binv(Binv), .Cin(ALUblock_1_cout), .CONJUNCT(CONJUNCT[1]),
    .DISJUNCT(DISJUNCT[1]), .XDISJUNCT(XDIJSJUNCT[1]), .Cout(ALUblock_2_cout), .SUM(SUM[1]));
  ALUblock ALUblock_3 (
    .A(A[2]), .Ainv(Ainv), .B(B[2]), .Binv(Binv), .Cin(ALUblock_2_cout), .CONJUNCT(CONJUNCT[2]),
    .DISJUNCT(DISJUNCT[2]), .XDISJUNCT(XDIJSJUNCT[2]), .Cout(ALUblock_3_cout), .SUM(SUM[2]));
  ALUblock ALUblock_4 (
    .A(A[3]), .Ainv(Ainv), .B(B[3]), .Binv(Binv), .Cin(ALUblock_3_cout), .CONJUNCT(CONJUNCT[3]),
    .DISJUNCT(DISJUNCT[3]), .XDISJUNCT(XDIJSJUNCT[3]), .Cout(ALUblock_4_cout), .SUM(SUM[3]));
  ALUblock ALUblock_5 (
    .A(A[4]), .Ainv(Ainv), .B(B[4]), .Binv(Binv), .Cin(ALUblock_4_cout), .CONJUNCT(CONJUNCT[4]),
    .DISJUNCT(DISJUNCT[4]), .XDISJUNCT(XDIJSJUNCT[4]), .Cout(ALUblock_5_cout), .SUM(SUM[4]));
  ALUblock ALUblock_6 (
    .A(A[5]), .Ainv(Ainv), .B(B[5]), .Binv(Binv), .Cin(ALUblock_5_cout), .CONJUNCT(CONJUNCT[5]),
    .DISJUNCT(DISJUNCT[5]), .XDISJUNCT(XDIJSJUNCT[5]), .Cout(ALUblock_6_cout), .SUM(SUM[5]));
  ALUblock ALUblock_7 (
    .A(A[6]), .Ainv(Ainv), .B(B[6]), .Binv(Binv), .Cin(ALUblock_6_cout), .CONJUNCT(CONJUNCT[6]),
    .DISJUNCT(DISJUNCT[6]), .XDISJUNCT(XDIJSJUNCT[6]), .Cout(ALUblock_7_cout), .SUM(SUM[6]));
  ALUblock ALUblock_8 (
    .A(A[7]), .Ainv(Ainv), .B(B[7]), .Binv(Binv), .Cin(ALUblock_7_cout), .CONJUNCT(CONJUNCT[7]),
    .DISJUNCT(DISJUNCT[7]), .XDISJUNCT(XDIJSJUNCT[7]), .Cout(Cout), .SUM(SUM[7]));
endmodule

module COMPUTETEST (
  input  [7:0] in_1,
  input  [7:0] in_2,
  input  in_3,
  input  in_4,
  input  in_5,
  output out_6,
  output [7:0] out_7,
  output [7:0] out_8,
  output [7:0] out_9,
  output [7:0] out_10
);

  COMPUTE compute_1 (
    .A(in_1), .B(in_2), .Ainv(in_3), .Binv(in_4), .Cin(in_5), .Cout(out_6), .CONJUNCT(out_7),
    .DISJUNCT(out_8), .XDIJSJUNCT(out_9), .SUM(out_10));
endmodule

module MLT8BIT (
  input  [7:0] A,
  input  [7:0] B,
  output [7:0] MLT,
  output V
);

  wire [6:0] and_58_out;
  wire [7:0] and_1_out, and_9_out, and_17_out, and_25_out, and_33_out, and_41_out, and_49_out,
       L_8_bit_adder_56e5dae9_1_out_3, L_8_bit_adder_56e5dae9_2_out_3, L_8_bit_adder_56e5dae9_3_out_3,
       L_8_bit_adder_56e5dae9_4_out_3, L_8_bit_adder_56e5dae9_5_out_3, L_8_bit_adder_56e5dae9_6_out_3,
       L_8_bit_adder_56e5dae9_7_out_3;

  // Probe on B
  // Probe on A
  and and_1 (and_1_out[0], A[7], B[0]);
  and and_2 (and_1_out[1], A[7], B[1]);
  and and_3 (and_1_out[2], A[7], B[2]);
  and and_4 (and_1_out[3], A[7], B[3]);
  and and_5 (and_1_out[4], A[7], B[4]);
  and and_6 (and_1_out[5], A[7], B[5]);
  and and_7 (and_1_out[6], A[7], B[6]);
  and and_8 (and_1_out[7], A[7], B[7]);
  or or_1 (V, L_8_bit_adder_56e5dae9_7_out_3[7], L_8_bit_adder_56e5dae9_7_out_3[6], L_8_bit_adder_56e5dae9_7_out_3[5], L_8_bit_adder_56e5dae9_7_out_3[4], L_8_bit_adder_56e5dae9_7_out_3[3], L_8_bit_adder_56e5dae9_7_out_3[2], L_8_bit_adder_56e5dae9_7_out_3[1], L_8_bit_adder_56e5dae9_7_out_3[0]);
  // Probe on and_1_out
  // Probe on and_1_out
  // Probe on L_8_bit_adder_56e5dae9_6_out_3
  L_8_bit_adder_56e5dae9 L_8_bit_adder_56e5dae9_7 (
    .out_3({L_8_bit_adder_56e5dae9_7_out_3, MLT[7]}), .in_1(L_8_bit_adder_56e5dae9_6_out_3), .in_2(and_1_out));
  and and_9 (and_9_out[0], A[6], B[0]);
  and and_10 (and_9_out[1], A[6], B[1]);
  and and_11 (and_9_out[2], A[6], B[2]);
  and and_12 (and_9_out[3], A[6], B[3]);
  and and_13 (and_9_out[4], A[6], B[4]);
  and and_14 (and_9_out[5], A[6], B[5]);
  and and_15 (and_9_out[6], A[6], B[6]);
  and and_16 (and_9_out[7], A[6], B[7]);
  // Probe on and_9_out
  // Probe on and_9_out
  // Probe on L_8_bit_adder_56e5dae9_5_out_3
  L_8_bit_adder_56e5dae9 L_8_bit_adder_56e5dae9_6 (
    .out_3({L_8_bit_adder_56e5dae9_6_out_3, MLT[6]}), .in_1(L_8_bit_adder_56e5dae9_5_out_3), .in_2(and_9_out));
  and and_17 (and_17_out[0], A[5], B[0]);
  and and_18 (and_17_out[1], A[5], B[1]);
  and and_19 (and_17_out[2], A[5], B[2]);
  and and_20 (and_17_out[3], A[5], B[3]);
  and and_21 (and_17_out[4], A[5], B[4]);
  and and_22 (and_17_out[5], A[5], B[5]);
  and and_23 (and_17_out[6], A[5], B[6]);
  and and_24 (and_17_out[7], A[5], B[7]);
  // Probe on and_17_out
  // Probe on and_17_out
  // Probe on L_8_bit_adder_56e5dae9_4_out_3
  L_8_bit_adder_56e5dae9 L_8_bit_adder_56e5dae9_5 (
    .out_3({L_8_bit_adder_56e5dae9_5_out_3, MLT[5]}), .in_1(L_8_bit_adder_56e5dae9_4_out_3), .in_2(and_17_out));
  and and_25 (and_25_out[0], A[4], B[0]);
  and and_26 (and_25_out[1], A[4], B[1]);
  and and_27 (and_25_out[2], A[4], B[2]);
  and and_28 (and_25_out[3], A[4], B[3]);
  and and_29 (and_25_out[4], A[4], B[4]);
  and and_30 (and_25_out[5], A[4], B[5]);
  and and_31 (and_25_out[6], A[4], B[6]);
  and and_32 (and_25_out[7], A[4], B[7]);
  // Probe on and_25_out
  // Probe on and_25_out
  // Probe on L_8_bit_adder_56e5dae9_3_out_3
  L_8_bit_adder_56e5dae9 L_8_bit_adder_56e5dae9_4 (
    .out_3({L_8_bit_adder_56e5dae9_4_out_3, MLT[4]}), .in_1(L_8_bit_adder_56e5dae9_3_out_3), .in_2(and_25_out));
  and and_33 (and_33_out[0], A[3], B[0]);
  and and_34 (and_33_out[1], A[3], B[1]);
  and and_35 (and_33_out[2], A[3], B[2]);
  and and_36 (and_33_out[3], A[3], B[3]);
  and and_37 (and_33_out[4], A[3], B[4]);
  and and_38 (and_33_out[5], A[3], B[5]);
  and and_39 (and_33_out[6], A[3], B[6]);
  and and_40 (and_33_out[7], A[3], B[7]);
  // Probe on and_33_out
  // Probe on and_33_out
  // Probe on L_8_bit_adder_56e5dae9_2_out_3
  L_8_bit_adder_56e5dae9 L_8_bit_adder_56e5dae9_3 (
    .out_3({L_8_bit_adder_56e5dae9_3_out_3, MLT[3]}), .in_1(L_8_bit_adder_56e5dae9_2_out_3), .in_2(and_33_out));
  and and_41 (and_41_out[0], A[2], B[0]);
  and and_42 (and_41_out[1], A[2], B[1]);
  and and_43 (and_41_out[2], A[2], B[2]);
  and and_44 (and_41_out[3], A[2], B[3]);
  and and_45 (and_41_out[4], A[2], B[4]);
  and and_46 (and_41_out[5], A[2], B[5]);
  and and_47 (and_41_out[6], A[2], B[6]);
  and and_48 (and_41_out[7], A[2], B[7]);
  // Probe on and_41_out
  // Probe on and_41_out
  // Probe on L_8_bit_adder_56e5dae9_1_out_3
  L_8_bit_adder_56e5dae9 L_8_bit_adder_56e5dae9_2 (
    .out_3({L_8_bit_adder_56e5dae9_2_out_3, MLT[2]}), .in_1(L_8_bit_adder_56e5dae9_1_out_3), .in_2(and_41_out));
  and and_49 (and_49_out[0], A[1], B[0]);
  and and_50 (and_49_out[1], A[1], B[1]);
  and and_51 (and_49_out[2], A[1], B[2]);
  and and_52 (and_49_out[3], A[1], B[3]);
  and and_53 (and_49_out[4], A[1], B[4]);
  and and_54 (and_49_out[5], A[1], B[5]);
  and and_55 (and_49_out[6], A[1], B[6]);
  and and_56 (and_49_out[7], A[1], B[7]);
  // Probe on and_49_out
  // Probe on and_49_out
  L_8_bit_adder_56e5dae9 L_8_bit_adder_56e5dae9_1 (
    .out_3({L_8_bit_adder_56e5dae9_1_out_3, MLT[1]}), .in_1({1'b0, and_58_out}), .in_2(and_49_out));
  and and_57 (MLT[0], A[0], B[0]);
  and and_58 (and_58_out[0], A[0], B[1]);
  and and_59 (and_58_out[1], A[0], B[2]);
  and and_60 (and_58_out[2], A[0], B[3]);
  and and_61 (and_58_out[3], A[0], B[4]);
  and and_62 (and_58_out[4], A[0], B[5]);
  and and_63 (and_58_out[5], A[0], B[6]);
  and and_64 (and_58_out[6], A[0], B[7]);
  // Probe on {1'b0, and_58_out}
  // Probe on {and_58_out, MLT[0]}
  // Probe on MLT

  // Notes on the sheet:
  //   OVERFLOW
endmodule

module ALU (
  input  [7:0] A,
  input  [7:0] B,
  input  [2:0] CTL,
  output OCN,
  output Z,
  output [7:0] RES,
  output V
);

  wire decoder_1_out4;
  wire [7:0] COMPUTE_1_conjunct, COMPUTE_1_disjunct, COMPUTE_1_sum, COMPUTE_1_xdijsjunct, MLT8BIT_1_mlt;

  Decoder #(.enable("false"), .select(3)) decoder_1 (
    .out4(decoder_1_out4), .sel(CTL));  // open: out0, out1, out2, out3, out5, out6, out7
  COMPUTE COMPUTE_1 (
    .A(A), .B(B), .Ainv(1'b0), .Binv(decoder_1_out4), .Cin(decoder_1_out4), .Cout(OCN),
    .CONJUNCT(COMPUTE_1_conjunct), .DISJUNCT(COMPUTE_1_disjunct), .XDIJSJUNCT(COMPUTE_1_xdijsjunct),
    .SUM(COMPUTE_1_sum));
  MLT8BIT MLT8BIT_1 (.A(A), .B(B), .MLT(MLT8BIT_1_mlt), .V(V));
  Multiplexer #(.enable("false"), .select(3), .width(8)) multiplexer_1 (
    .in0(COMPUTE_1_conjunct), .in1(COMPUTE_1_disjunct), .in2(COMPUTE_1_xdijsjunct), .in3(COMPUTE_1_sum),
    .in4(COMPUTE_1_sum), .in5(MLT8BIT_1_mlt), .in6({8{1'b0}}), .in7({8{1'b0}}), .out(RES), .sel(CTL));
  nor nor_1 (Z, RES[0], RES[1], RES[2], RES[3], RES[4], RES[5], RES[6], RES[7]);
endmodule

module CPU (
  output S_RESET,
  output S_CLK,
  output S_WRITE,
  output [4:0] S_X,
  output [4:0] S_Y,
  output [23:0] S_DATA
);

  wire alu_1_ocn, alu_1_v, alu_1_z, and_3_out, C2_q, C2_qn, C_q, C_qn, clock_1_out, comparator_1_eq,
       decoder_1_out0, decoder_1_out1, decoder_1_out2, decoder_1_out3, decoder_1_out4, decoder_1_out5,
       decoder_1_out6, decoder_1_out7, decoder_2_out1, decoder_2_out2, decoder_2_out3, decoder_2_out4,
       decoder_2_out5, decoder_2_out6, decoder_2_out7, decoder_2_out8, decoder_2_out9, decoder_2_out10,
       decoder_2_out11, decoder_2_out12, decoder_2_out13, decoder_2_out14, decoder_2_out15,
       multiplexer_2_out, or_1_out, or_3_out, or_4_out, shh2_1_data, shh2_1_inc, shhh_1_x, shhh_1_y, V2_q,
       V2_qn, V_q, V_qn, Z2_q, Z2_qn, Z_q, Z_qn;
  wire [2:0] multiplexer_5_out_4;
  wire [3:0] d_ff_1_q, multiplexer_5_out, multiplexer_5_out_2;
  wire [7:0] alu_1_res, C_ADDR, MICROCODE_ADDRESS, multiplexer_1_out, multiplexer_3_out, multiplexer_4_out,
       R2_q, R3_q, R4_q, R5_q, R6_q, R7_q, R8LINE, R9LINE, R10LINE, R11LINE, R12LINE, R13LINE, R14LINE,
       R15LINE, ram_1_dout, register_1_q, rom_1_data;
  wire [15:0] and_1_out, and_2_out, linecloner16_1_out_2, linecloner16_2_out_2, or_2_out;
  wire [17:8] multiplexer_5_out_3;
  wire [28:0] instructiondecoder_1_out_3, MICROCODE_INSTRUCTION, rom_2_data;

  Clock clock_1 (.out(clock_1_out));
  InstructionDecoder instructiondecoder_1 (
    .out_3(instructiondecoder_1_out_3), .in_2(MICROCODE_ADDRESS), .in_1({R14LINE, R15LINE}));
  RAM #(.addrWidth(16)) ram_1 (
    .addr(or_2_out), .we(shhh_1_x), .oe(shhh_1_y), .clk(or_1_out), .din(alu_1_res), .dout(ram_1_dout));
  or or_1 (or_1_out, shhh_1_y, clock_1_out);
  ROM #(.addrWidth(16)) rom_1 (.addr(or_2_out), .data(rom_1_data));
  assign or_2_out = and_1_out | and_2_out;  // OR_Gate or_2, 16 bits wide
  Register #(.width(29)) MICROCODE_INSTRUCTION_REGISTER (
    .D(instructiondecoder_1_out_3), .en(decoder_1_out7), .clk(clock_1_out), .Q(MICROCODE_INSTRUCTION));  // open: clr
  assign and_1_out = {R9LINE, R8LINE} & linecloner16_1_out_2;  // AND_Gate and_1, 16 bits wide
  assign and_2_out = {R11LINE, R10LINE} & linecloner16_2_out_2;  // AND_Gate and_2, 16 bits wide
  DISPLAY_CONTROLLER display_controller_1 (
    .S_RESET(S_RESET), .S_CLK(S_CLK), .S_WRITE(S_WRITE), .S_X(S_X), .S_Y(S_Y), .S_DATA(S_DATA),
    .MICROCODE_ADDR(C_ADDR), .R(R15LINE), .G(R14LINE), .B(R13LINE), .CPU_CLK(clock_1_out));
  linecloner16 linecloner16_1 (.in_1(or_3_out), .out_2(linecloner16_1_out_2));
  linecloner16 linecloner16_2 (.in_1(or_4_out), .out_2(linecloner16_2_out_2));
  or or_3 (or_3_out, decoder_1_out4, decoder_1_out3, decoder_1_out2, decoder_1_out1, decoder_1_out0);
  or or_4 (or_4_out, decoder_1_out5, decoder_1_out6);
  Register R15INT2 (.D(multiplexer_1_out), .en(decoder_2_out15), .clk(clock_1_out), .Q(R15LINE));  // open: clr
  Register R14INT1 (.D(multiplexer_1_out), .en(decoder_2_out14), .clk(clock_1_out), .Q(R14LINE));  // open: clr
  Decoder #(.enable("false"), .select(3)) decoder_1 (
    .out0(decoder_1_out0), .out1(decoder_1_out1), .out2(decoder_1_out2), .out3(decoder_1_out3),
    .out4(decoder_1_out4), .out5(decoder_1_out5), .out6(decoder_1_out6), .out7(decoder_1_out7),
    .sel(multiplexer_5_out_3[17:15]));
  Multiplexer #(.enable("false"), .select(3), .width(8)) multiplexer_1 (
    .in0(alu_1_res), .in1(ram_1_dout), .in2(alu_1_res), .in3(rom_1_data), .in4(MICROCODE_ADDRESS),
    .in5(alu_1_res), .in6(rom_1_data), .out(multiplexer_1_out), .sel(multiplexer_5_out_3[17:15]));  // open: in7
  // Probe on multiplexer_5_out_3[17:15]
  shhh shhh_1 (
    .c(multiplexer_5_out_3[17]), .a(multiplexer_5_out_3[16]), .b(multiplexer_5_out_3[15]), .x(shhh_1_x),
    .y(shhh_1_y));
  Register R13SPECIAL (.D(multiplexer_1_out), .en(decoder_2_out13), .clk(clock_1_out), .Q(R13LINE));  // open: clr
  Register R12SP (.D(multiplexer_1_out), .en(decoder_2_out12), .clk(clock_1_out), .Q(R12LINE));  // open: clr
  Register R11PC2 (.D(multiplexer_1_out), .en(decoder_2_out11), .clk(clock_1_out), .Q(R11LINE));  // open: clr
  Register R10PC1 (.D(multiplexer_1_out), .en(decoder_2_out10), .clk(clock_1_out), .Q(R10LINE));  // open: clr
  Register R9ADDR2 (.D(multiplexer_1_out), .en(decoder_2_out9), .clk(clock_1_out), .Q(R9LINE));  // open: clr
  Register R8ADDR1 (.D(multiplexer_1_out), .en(decoder_2_out8), .clk(clock_1_out), .Q(R8LINE));  // open: clr
  // Probe on multiplexer_1_out
  Decoder #(.select(4)) decoder_2 (
    .out1(decoder_2_out1), .out2(decoder_2_out2), .out3(decoder_2_out3), .out4(decoder_2_out4),
    .out5(decoder_2_out5), .out6(decoder_2_out6), .out7(decoder_2_out7), .out8(decoder_2_out8),
    .out9(decoder_2_out9), .out10(decoder_2_out10), .out11(decoder_2_out11), .out12(decoder_2_out12),
    .out13(decoder_2_out13), .out14(decoder_2_out14), .out15(decoder_2_out15), .sel(multiplexer_5_out_3[11:8]));  // open: out0, en
  // Probe on multiplexer_5_out_3[11:8]
  D_Flip_Flop C (.clk(clock_1_out), .D(alu_1_ocn), .Q(C_q), .Qn(C_qn));  // open: preset, reset
  D_Flip_Flop Z (.clk(clock_1_out), .D(alu_1_z), .Q(Z_q), .Qn(Z_qn));  // open: preset, reset
  D_Flip_Flop V (.clk(clock_1_out), .D(alu_1_v), .Q(V_q), .Qn(V_qn));  // open: preset, reset
  and and_3 (and_3_out, clock_1_out, ~comparator_1_eq, d_ff_1_q[3]);  // AND_Gate
  D_Flip_Flop C2 (.clk(and_3_out), .D(alu_1_ocn), .Q(C2_q), .Qn(C2_qn));  // open: preset, reset
  D_Flip_Flop Z2 (.clk(and_3_out), .D(alu_1_z), .Q(Z2_q), .Qn(Z2_qn));  // open: preset, reset
  D_Flip_Flop V2 (.clk(and_3_out), .D(alu_1_v), .Q(V2_q), .Qn(V2_qn));  // open: preset, reset
  Register register_1 (.D(multiplexer_1_out), .en(decoder_2_out1), .clk(clock_1_out), .Q(register_1_q));  // open: clr
  Register R2 (.D(multiplexer_1_out), .en(decoder_2_out2), .clk(clock_1_out), .Q(R2_q));  // open: clr
  Register R3 (.D(multiplexer_1_out), .en(decoder_2_out3), .clk(clock_1_out), .Q(R3_q));  // open: clr
  Register R4 (.D(multiplexer_1_out), .en(decoder_2_out4), .clk(clock_1_out), .Q(R4_q));  // open: clr
  Register R5 (.D(multiplexer_1_out), .en(decoder_2_out5), .clk(clock_1_out), .Q(R5_q));  // open: clr
  Register R6 (.D(multiplexer_1_out), .en(decoder_2_out6), .clk(clock_1_out), .Q(R6_q));  // open: clr
  Register R7 (.D(multiplexer_1_out), .en(decoder_2_out7), .clk(clock_1_out), .Q(R7_q));  // open: clr
  shh2 shh2_1 (.MUX(multiplexer_2_out), .EXEC(decoder_1_out7), .DATA(shh2_1_data), .INC(shh2_1_inc));
  Multiplexer #(.enable("false"), .select(4)) multiplexer_2 (
    .in0(1'b0), .in1(1'b1), .in2(C_q), .in3(C_qn), .in4(Z_q), .in5(Z_qn), .in6(V_q), .in7(V_qn), .in8(1'b0),
    .in9(1'b1), .in10(C2_q), .in11(C2_qn), .in12(Z2_q), .in13(Z2_qn), .in14(V2_q), .in15(V2_qn),
    .out(multiplexer_2_out), .sel(d_ff_1_q));
  // Probe on d_ff_1_q
  // Probe on MICROCODE_ADDRESS
  Counter #(.trigger("falling")) counter_1 (
    .load(shh2_1_data), .D(MICROCODE_ADDRESS), .count(shh2_1_inc), .Q(C_ADDR), .clk(clock_1_out));  // open: carry, up, clr
  ROM #(.dataWidth(29)) rom_2 (.addr(C_ADDR), .data(rom_2_data));
  Multiplexer #(.enable("false"), .select(4), .width(8)) multiplexer_3 (
    .in0({8{1'b0}}), .in1(register_1_q), .in2(R2_q), .in3(R3_q), .in4(R4_q), .in5(R5_q), .in6(R6_q),
    .in7(R7_q), .in8(R8LINE), .in9(R9LINE), .in10(R10LINE), .in11(R11LINE), .in12(R12LINE), .in13(R13LINE),
    .in14(R14LINE), .in15(R15LINE), .out(multiplexer_3_out), .sel(multiplexer_5_out));
  Multiplexer #(.enable("false"), .select(4), .width(8)) multiplexer_4 (
    .in0({8{1'b0}}), .in1(register_1_q), .in2(R2_q), .in3(R3_q), .in4(R4_q), .in5(R5_q), .in6(R6_q),
    .in7(R7_q), .in8(R8LINE), .in9(R9LINE), .in10(R10LINE), .in11(R11LINE), .in12(R12LINE), .in13(R13LINE),
    .in14(R14LINE), .in15(R15LINE), .out(multiplexer_4_out), .sel(multiplexer_5_out_2));
  D_Flip_Flop #(.trigger("falling")) d_ff_1 (
    .D(decoder_1_out7), .clk(clock_1_out), .Q(d_ff_1_q[3]));  // open: Qn, preset, reset
  Multiplexer #(.enable("false"), .width(29)) multiplexer_5 (
    .in0(rom_2_data), .in1(MICROCODE_INSTRUCTION),
    .out({MICROCODE_ADDRESS, d_ff_1_q[2:0], multiplexer_5_out_3[17:15], multiplexer_5_out_4, multiplexer_5_out_3[11:8], multiplexer_5_out_2, multiplexer_5_out}),
    .sel(d_ff_1_q[3]));
  ALU alu_1 (
    .A(multiplexer_3_out), .B(multiplexer_4_out), .CTL(multiplexer_5_out_4), .OCN(alu_1_ocn), .Z(alu_1_z),
    .RES(alu_1_res), .V(alu_1_v));
  // Probe on {MICROCODE_ADDRESS, d_ff_1_q[2:0], multiplexer_5_out_3[17:15], multiplexer_5_out_4, multiplexer_5_out_3[11:8], multiplexer_5_out_2, multiplexer_5_out}
  Comparator #(.mode("unsigned"), .width(4)) comparator_1 (
    .a(4'b0000), .b(multiplexer_5_out), .eq(comparator_1_eq));  // open: gt, lt

  // Notes on the sheet:
  //   contents of rom_1 (hex, n*v repeats v):
  //   bf 2b 0 4b 0 6b 2 39 0 6a bf 2b 0 4b 0 6b 2 39 0 6a bf 2b 0 4b 0 6b 2 39 0 6a bf 2b 0 4b 0 6b 2 39 0
  //   6a bf 2b 0 4b 0 6b 2 39 0 6a bf 2b 0 4b 0 6b 2 39 0 6a bf 2b 0 4b 0 6b 2 39 0 6a bf 2b 0 4b 0 6b 2
  //   39 0 6a bf 2b 0 4b 0 6b 2 39 0 6a bf 2b 0 4b 0 6b 2 39 0 6a bf 2b 0 4b 0 6b 2 39 0 6a bf 2b 0 4b 0
  //   6b 2 39 0 6a bf 2b 0 4b 0 6b 2 39 0 6a bf 2b 0 4b 0 6b 2 39 0 6a bf 2b 0 4b 0 6b 2 39 0 6a bf 2b 0
  //   4b 0 6b 2 39 0 6a bf 2b 0 4b 0 6b 2 39 0 6a bf 2b 0 4b 0 6b 2 39 0 6a bf 2b 0 4b 0 6b 2 39 0 6a bf
  //   2b 0 4b 0 6b 2 39 0 6a bf 2b 0 4b 0 6b 2 39 0 6a bf 2b 0 4b 0 6b 2 39 0 6a bf 2b 0 4b 0 6b 2 39 0 6a
  //   bf 2b 0 4b 0 6b 2 39 0 6a bf 2b 0 4b 0 6b 2 39 0 6a bf 2b 0 4b 0 6b 2 39 0 6a bf 2b 0 4b 0 6b 2 39 0
  //   6a bf 2b 0 4b 0 6b 2 39 0 6a bf 2b 0 4b 0 6b 2 39 0 6a bf 2b 0 4b 0 6b 2 39 0 6a bf 2b 0 4b 0 6b 2
  //   39 0 6a bf 2b 0 4b 0 6b 2 39 0 6a bf 2b 0 4b 0 6b 2 39 0 6a bf 2b 0 4b 0 6b 2 39 0 6a bf 2b 0 4b 0
  //   6b 2 39 0 6a bf 2b 0 4b 0 6b 2 39 0 6a bf 2b 0 4b 0 6b 2 39 0 6a bf 2b 0 4b 0 6b 2 39 0 6a bf 2b 0
  //   4b 0 6b 2 39 0 6a bf 2b 0 4b 0 6b 2 39 0 6a bf 2b 0 4b 0 6b 2 39 0 6a bf 2b 0 4b 0 6b 2 39 0 6a bf
  //   2b 0 4b 0 6b 2 39 0 6a bf 2b 0 4b 0 6b 2 39 0 6a bf 2b 0 4b 0 6b 2 39 0 6a bf 2b 0 4b 0 6b 2 39 0 6a
  //   bf 2b 0 4b 0 6b 2 39 0 6a bf 2b 0 4b 0 6b 2 39 0 6a bf 2b 0 4b 0 6b 2 39 0 6a bf 2b 0 4b 0 6b 2 39 0
  //   6a bf 2b 0 4b 0 6b 2 39 0 6a bf 2b 0 4b 0 6b 2 39 0 6a bf 2b 0 4b 0 6b 2 39 0 6a bf 2b 0 4b 0 6b 2
  //   39 0 6a bf 2b 0 4b 0 6b 2 39 0 6a bf 2b 0 4b 0 6b 2 39 0 6a bf 2b 0 4b 0 6b 2 39 0 6a bf 2b 0 4b 0
  //   6b 2 39 0 6a bf 2b 0 4b 0 6b 2 39 0 6a bf 2b 0 4b 0 6b 2 39 0 6a bf 2b 0 4b 0 6b 2 39 0 6a bf 2b 0
  //   4b 0 6b 2 39 0 6a bf 2b 0 4b 0 6b 2 39 0 6a bf 2b 0 4b 0 6b 2 39 0 6a bf 2b 0 4b 0 6b 2 39 0 6a bf
  //   2b 0 4b 0 6b 2 39 0 6a bf 2b 0 4b 0 6b 2 39 0 6a bf 2b 0 4b 0 6b 2 39 0 6a bf 2b 0 4b 0 6b 2 39 0 6a
  //   bf 2b 0 4b 0 6b 2 39 0 6a bf 2b 0 4b 0 6b 2 39 0 6a bf 2b 0 4b 0 6b 2 39 0 6a bf 2b 0 4b 0 6b 2 39 0
  //   6a bf 2b 0 4b 0 6b 2 39 0 6a bf 2b 0 4b 0 6b 2 39 0 6a bf 2b 0 4b 0 6b 2 39 0 6a bf 2b 0 4b 0 6b 2
  //   39 0 6a bf 2b 0 4b 0 6b 2 39 0 6a bf 2b 0 4b 0 6b 2 39 0 6a bf 2b 0 4b 0 6b 2 39 0 6a bf 2b 0 4b 0
  //   6b 2 39 0 6a bf 2b 0 4b 0 6b 2 39 0 6a bf 2b 0 4b 0 6b 2 39 0 6a bf 2b 0 4b 0 6b 2 39 0 6a bf 2b 0
  //   4b 0 6b 2 39 0 6a bf 2b 0 4b 0 6b 2 39 0 6a bf 2b 0 4b 0 6b 2 39 0 6a bf 2b 0 4b 0 6b 2 39 0 6a bf
  //   2b 0 4b 0 6b 2 39 0 6a bf 2b 0 4b 0 6b 2 39 0 6a bf 2b 0 4b 0 6b 2 39 0 6a bf 2b 0 4b 0 6b 2 39 0 6a
  //   bf 2b 0 4b 0 6b 2 39 0 6a bf 2b 0 4b 0 6b 2 39 0 6a bf 2b 0 4b 0 6b 2 39 0 6a bf 2b 0 4b 0 6b 2 39 0
  //   6a bf 2b 0 4b 0 6b 2 39 0 6a bf 2b 0 4b 0 6b 2 39 0 6a bf 2b 0 4b 0 6b 2 39 0 6a bf 2b 0 4b 0 6b 2
  //   39 0 6a bf 2b 0 4b 0 6b 2 39 0 6a bf 2b 0 4b 0 6b 2 39 0 6a bf 2b 0 4b 0 6b 2 39 0 6a bf 2b 0 4b 0
  //   6b 2 39 0 6a bf 2b 0 4b 0 6b 2 39 0 6a bf 2b 0 4b 0 6b 2 39 0 6a bf 2b 0 4b 0 6b 2 39 0 6a bf 2b 0
  //   4b 0 6b 2 39 0 6a bf 2b 0 4b 0 6b 2 39 0 6a bf 2b 0 4b 0 6b 2 39 0 6a bf 2b 0 4b 0 6b 2 39 0 6a bf
  //   2b 0 4b 0 6b 2 39 0 6a bf 2b 0 4b 0 6b 2 39 0 6a bf 2b 0 4b 0 6b 2 39 0 6a bf 2b 0 4b 0 6b 2 39 0 6a
  //   bf 2b 0 4b 0 6b 2 39 0 6a bf 2b 0 4b 0 6b 2 39 0 6a bf 2b 0 4b 0 6b 2 39 0 6a bf 2b 0 4b 0 6b 2 39 0
  //   6a bf 2b 0 4b 0 6b 2 39 0 6a bf 2b 0 4b 0 6b 2 39 0 6a bf 2b 0 4b 0 6b 2 39 0 6a bf 2b 0 4b 0 6b 2
  //   39 0 6a bf 2b 0 4b 0 6b 2 39 0 6a bf 2b 0 4b 0 6b 2 39 0 6a bf 2b 0 4b 0 6b 2 39 0 6a bf 2b 0 4b 0
  //   6b 2 39 0 6a bf 2b 0 4b 0 6b 2 39 0 6a bf 2b 0 4b 0 6b 2 39 0 6a bf 2b 0 4b 0 6b 2 39 0 6a bf 2b 0
  //   4b 0 6b 2 39 0 6a bf 2b 0 4b 0 6b 2 39 0 6a bf 2b 0 4b 0 6b 2 39 0 6a bf 2b 0 4b 0 6b 2 39 0 6a bf
  //   2b 0 4b 0 6b 2 39 0 6a bf 2b 0 4b 0 6b 2 39 0 6a bf 2b 0 4b 0 6b 2 39 0 6a bf 2b 0 4b 0 6b 2 39 0 6a
  //   bf 2b 0 4b 0 6b 2 39 0 6a bf 2b 0 4b 0 6b 2 39 0 6a bf 2b 0 4b 0 6b 2 39 0 6a bf 2b 0 4b 0 6b 2 39 0
  //   6a bf 2b 0 4b 0 6b 2 39 0 6a bf 2b 0 4b 0 6b 2 39 0 6a bf 2b 0 4b 0 6b 2 39 0 6a bf 2b 0 4b 0 6b 2
  //   39 0 6a bf 2b 0 4b 0 6b 2 39 0 6a bf 2b 0 4b 0 6b 2 39 0 6a bf 2b 0 4b 0 6b 2 39 0 6a bf 2b 0 4b 0
  //   6b 2 39 0 6a bf 2b 0 4b 0 6b 2 39 0 6a bf 2b 0 4b 0 6b 2 39 0 6a bf 2b 0 4b 0 6b 2 39 0 6a bf 2b 0
  //   4b 0 6b 2 39 0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
  //   contents of rom_2 (hex, n*v repeats v):
  //   220d00 30e00 b43ada 20a00 3bdb 30f00 38000 11440000 3800 11443900 3810 11443900 3820 11443900 3830
  //   11443900 3840 11443900 3850 11443900 3860 11443900 3870 11443900 3800 11443910 3810 11443910 3820
  //   11443910 3830 11443910 3840 11443910 3850 11443910 3860 11443910 3870 11443910 3800 11443920 3810
  //   11443920 3820 11443920 3830 11443920 3840 11443920 3850 11443920 3860 11443920 3870 11443920 3800
  //   11443930 3810 11443930 3820 11443930 3830 11443930 3840 11443930 3850 11443930 3860 11443930 3870
  //   11443930 3800 11443940 3810 11443940 3820 11443940 3830 11443940 3840 11443940 3850 11443940 3860
  //   11443940 3870 11443940 3800 11443950 3810 11443950 3820 11443950 3830 11443950 3840 11443950 3850
  //   11443950 3860 11443950 3870 11443950 3800 11443960 3810 11443960 3820 11443960 3830 11443960 3840
  //   11443960 3850 11443960 3860 11443960 3870 11443960 3800 11443970 3810 11443970 3820 11443970 3830
  //   11443970 3840 11443970 3850 11443970 3860 11443970 3870 11443970 3a80 43b90 143ada 20a00 43bdb 3e80
  //   3f90 16420900 38c0 1100a 3cdc 38c0 1100b 3cdc 38e0 114439f0 3e80 3f90 16420900 38c0 1100e 3cdc 38c0
  //   1100f 3cdc 38e0 114439f0 3e80 3f90 16420900 38c0 4cdc 8b00 4cdc 8a00 38e0 114439f0 3e80 3f90
  //   16420900 38c0 4cdc 8100 4cdc 8200 38e0 114439f0 20800 16620900 8f00 17b438d8 20800 39d9 8e00
  //   183438d8 20800 39d9 8d00 220d00 18d438d8 20800 39d9 17e20d00 194c40d9 220d00 11440000 220d00
  //   17240000
endmodule

module Thingy (
);

  CPU cpu_1 ();  // open: S_RESET, S_CLK, S_WRITE, S_X, S_Y, S_DATA
endmodule

module shhh (
  input  c,
  input  a,
  input  b,
  output x,
  output y
);

  wire not_1_out, not_2_out, not_3_out;

  not not_1 (not_1_out, c);
  not not_2 (not_2_out, a);
  not not_3 (not_3_out, b);
  and and_1 (x, not_1_out, a, not_3_out);
  and and_2 (y, not_1_out, not_2_out, b);
endmodule

module linecloner16 (
  input  in_1,
  output [15:0] out_2
);


  assign out_2 = {16{in_1}};
endmodule

module InstructionDecoder (
  input  [15:0] in_1,
  input  [7:0] in_2,
  output [28:0] out_3
);

  wire [28:0] aluop_decoder_1_microinstruction, draw_decoder_1_microinstruction,
       jump_decoder_1_microinstruction, loadstore_decoder_1_microinstruction,
       pushpop_decoder_1_microinstruction, set_decoder_1_microinstruction, setaddr_decoder_1_microinstruction;

  ALUOP_DECODER aluop_decoder_1 (
    .INSTRUCTION(in_1), .MICROINSTRUCTION_ADDRESS(in_2), .MICROINSTRUCTION(aluop_decoder_1_microinstruction));
  LOADSTORE_DECODER loadstore_decoder_1 (
    .INSTRUCTION(in_1), .MICROINSTRUCTION_ADDRESS(in_2),
    .MICROINSTRUCTION(loadstore_decoder_1_microinstruction));
  SET_DECODER set_decoder_1 (
    .INSTRUCTION(in_1), .MICROINSTRUCTION_ADDRESS(in_2), .MICROINSTRUCTION(set_decoder_1_microinstruction));
  JUMP_DECODER jump_decoder_1 (
    .INSTRUCTION(in_1), .MICROINSTRUCTION_ADDRESS(in_2), .MICROINSTRUCTION(jump_decoder_1_microinstruction));
  SETADDR_DECODER setaddr_decoder_1 (
    .INSTRUCTION(in_1), .MICROINSTRUCTION_ADDRESS(in_2), .MICROINSTRUCTION(setaddr_decoder_1_microinstruction));
  PUSHPOP_DECODER pushpop_decoder_1 (
    .INSTRUCTION(in_1), .MICROINSTRUCTION_ADDRESS(in_2), .MICROINSTRUCTION(pushpop_decoder_1_microinstruction));
  DRAW_DECODER draw_decoder_1 (.MICROINSTRUCTION(draw_decoder_1_microinstruction));
  Multiplexer #(.enable("false"), .select(5), .width(29)) multiplexer_1 (
    .in0(aluop_decoder_1_microinstruction), .in1(aluop_decoder_1_microinstruction),
    .in2(aluop_decoder_1_microinstruction), .in3(aluop_decoder_1_microinstruction),
    .in4(aluop_decoder_1_microinstruction), .in5(aluop_decoder_1_microinstruction),
    .in6(aluop_decoder_1_microinstruction), .in7(aluop_decoder_1_microinstruction),
    .in8(loadstore_decoder_1_microinstruction), .in9(loadstore_decoder_1_microinstruction),
    .in10(loadstore_decoder_1_microinstruction), .in11(set_decoder_1_microinstruction),
    .in12(jump_decoder_1_microinstruction), .in13(jump_decoder_1_microinstruction),
    .in14(jump_decoder_1_microinstruction), .in15(jump_decoder_1_microinstruction),
    .in16(jump_decoder_1_microinstruction), .in17(jump_decoder_1_microinstruction),
    .in18(jump_decoder_1_microinstruction), .in19(jump_decoder_1_microinstruction),
    .in20(jump_decoder_1_microinstruction), .in21(pushpop_decoder_1_microinstruction),
    .in22(pushpop_decoder_1_microinstruction), .in23(pushpop_decoder_1_microinstruction),
    .in24(pushpop_decoder_1_microinstruction), .in25(setaddr_decoder_1_microinstruction),
    .in26(draw_decoder_1_microinstruction), .out(out_3), .sel(in_1[4:0]));  // open: in27, in28, in29, in30, in31
endmodule

module ALUOP_DECODER (
  input  [15:0] INSTRUCTION,
  input  [7:0] MICROINSTRUCTION_ADDRESS,
  output [28:0] MICROINSTRUCTION
);

  assign MICROINSTRUCTION[11:8] = {{1{1'b0}}, INSTRUCTION[7:5]};  // Bit_Extender bit_extender_1
  assign MICROINSTRUCTION[7:4] = {{1{1'b0}}, INSTRUCTION[10:8]};  // Bit_Extender bit_extender_2

  assign {MICROINSTRUCTION[28:12], MICROINSTRUCTION[3:0]} = {MICROINSTRUCTION_ADDRESS, {6{1'b0}}, INSTRUCTION[2:0], MICROINSTRUCTION[11:8]};
endmodule

module LOADSTORE_DECODER (
  input  [15:0] INSTRUCTION,
  input  [7:0] MICROINSTRUCTION_ADDRESS,
  output [28:0] MICROINSTRUCTION
);

  assign MICROINSTRUCTION[11:8] = {{1{1'b0}}, INSTRUCTION[7:5]};  // Bit_Extender bit_extender_1
  Multiplexer #(.enable("false"), .select(5), .width(3)) multiplexer_1 (
    .in8(3'b001), .in9(3'b011), .in10(3'b010), .out(MICROINSTRUCTION[17:15]), .sel(INSTRUCTION[4:0]));  // open: in0, in1, in2, in3, in4, in5, in6, in7, in11, in12, in13, in14, in15, in16, in17, in18, in19, in20, in21, in22, in23, in24, in25, in26, in27, in28, in29, in30, in31

  assign {MICROINSTRUCTION[28:18], MICROINSTRUCTION[14:12], MICROINSTRUCTION[7:0]} = {MICROINSTRUCTION_ADDRESS, 6'b000001, MICROINSTRUCTION[11:8], 4'b0000};
endmodule

module SET_DECODER (
  input  [15:0] INSTRUCTION,
  input  [7:0] MICROINSTRUCTION_ADDRESS,
  output [28:0] MICROINSTRUCTION
);

  assign MICROINSTRUCTION[11:8] = {{1{1'b0}}, INSTRUCTION[7:5]};  // Bit_Extender bit_extender_1

  assign {MICROINSTRUCTION[28:12], MICROINSTRUCTION[7:0]} = {INSTRUCTION[15:8], 17'h2000};
endmodule

module JUMP_DECODER (
  input  [15:0] INSTRUCTION,
  input  [7:0] MICROINSTRUCTION_ADDRESS,
  output [28:0] MICROINSTRUCTION
);

  Multiplexer #(.enable("false"), .select(5), .width(3)) multiplexer_1 (
    .in12(3'b001), .in13(3'b010), .in14(3'b011), .in15(3'b100), .in16(3'b101), .in17(3'b110), .in18(3'b111),
    .in19(3'b001), .in20(3'b001), .out(MICROINSTRUCTION[20:18]), .sel(INSTRUCTION[4:0]));  // open: in0, in1, in2, in3, in4, in5, in6, in7, in8, in9, in10, in11, in21, in22, in23, in24, in25, in26, in27, in28, in29, in30, in31

  assign {MICROINSTRUCTION[28:21], MICROINSTRUCTION[17:0]} = 26'h2200000;
endmodule

module SETADDR_DECODER (
  input  [15:0] INSTRUCTION,
  input  [7:0] MICROINSTRUCTION_ADDRESS,
  output [28:0] MICROINSTRUCTION
);

  PLA #(.in_width(6), .out_width(8), .\table ("000000 00001000\n001000 00001010\n010000 00001100\n011000 00001110\n100000 00010000\n101000 00010010\n110000 00010100\n111000 00010110\n000001 00011000\n001001 00011010\n010001 00011100\n011001 00011110\n100001 00100000\n101001 00100010\n110001 00100100\n111001 00100110\n000010 00101000\n001010 00101010\n010010 00101100\n011010 00101110\n100010 00110000\n101010 00110010\n110010 00110100\n111010 00110110\n000011 00111000\n001011 00111010\n010011 00111100\n011011 00111110\n100011 01000000\n101011 01000010\n110011 01000100\n111011 01000110\n000100 01001000\n001100 01001010\n010100 01001100\n011100 01001110\n100100 01010000\n101100 01010010\n110100 01010100\n111100 01010110\n000101 01011000\n001101 01011010\n010101 01011100\n011101 01011110\n100101 01100000\n101101 01100010\n110101 01100100\n111101 01100110\n000110 01101000\n001110 01101010\n010110 01101100\n011110 01101110\n100110 01110000\n101110 01110010\n110110 01110100\n111110 01110110\n000111 01111000\n001111 01111010\n010111 01111100\n011111 01111110\n100111 10000000\n101111 10000010\n110111 10000100\n111111 10000110")) pla_1 (
    .in(INSTRUCTION[10:5]), .out(MICROINSTRUCTION[28:21]));

  assign MICROINSTRUCTION[20:0] = 21'h40000;
endmodule

module shh2 (
  input  MUX,
  input  EXEC,
  output DATA,
  output INC
);

  wire not_1_out, not_2_out;

  not not_1 (not_1_out, MUX);
  not not_2 (not_2_out, EXEC);
  and and_1 (INC, not_1_out, not_2_out);

  assign DATA = MUX;
endmodule

module COMPUTER (
);

  wire cpu_1_s_clk, cpu_1_s_reset, cpu_1_s_write;
  wire [4:0] cpu_1_s_x, cpu_1_s_y;
  wire [23:0] cpu_1_s_data;

  CPU cpu_1 (
    .S_RESET(cpu_1_s_reset), .S_CLK(cpu_1_s_clk), .S_WRITE(cpu_1_s_write), .S_X(cpu_1_s_x), .S_Y(cpu_1_s_y),
    .S_DATA(cpu_1_s_data));
  // RGB_Video #(.height(32), .scale(7), .width(32)) rgb_video_1: pin names not known; wires that end beside it: cpu_1_s_reset, cpu_1_s_clk, cpu_1_s_write, cpu_1_s_x, cpu_1_s_y, cpu_1_s_data
endmodule

module PUSHPOP_DECODER (
  input  [15:0] INSTRUCTION,
  input  [7:0] MICROINSTRUCTION_ADDRESS,
  output [28:0] MICROINSTRUCTION
);

  Multiplexer #(.enable("false"), .select(5), .width(8)) multiplexer_1 (
    .in21(8'h8d), .in22(8'h98), .in23(8'ha3), .in24(8'had), .out(MICROINSTRUCTION[28:21]),
    .sel(INSTRUCTION[4:0]));  // open: in0, in1, in2, in3, in4, in5, in6, in7, in8, in9, in10, in11, in12, in13, in14, in15, in16, in17, in18, in19, in20, in25, in26, in27, in28, in29, in30, in31

  assign MICROINSTRUCTION[20:0] = 21'h40000;
endmodule

module DRAW_DECODER (
  output [28:0] MICROINSTRUCTION
);


  assign MICROINSTRUCTION = 29'h16e40000;
endmodule

module DISPLAY_CONTROLLER (
  input  [7:0] R,
  input  [7:0] G,
  input  [7:0] B,
  input  [7:0] MICROCODE_ADDR,
  input  CPU_CLK,
  output S_RESET,
  output S_CLK,
  output S_WRITE,
  output [4:0] S_X,
  output [4:0] S_Y,
  output [23:0] S_DATA
);

  wire and_1_out, comparator_3_eq, counter_1_carry, not_1_out, YCOUNT_carry;

  Comparator comparator_1 (.a(MICROCODE_ADDR), .b(8'hb7), .eq(S_RESET));  // open: gt, lt
  Comparator comparator_2 (.a(MICROCODE_ADDR), .b(8'hc2), .eq(S_WRITE));  // open: gt, lt
  Comparator comparator_3 (.a(MICROCODE_ADDR), .b(8'hc3), .eq(comparator_3_eq));  // open: gt, lt
  not not_1 (not_1_out, YCOUNT_carry);
  and and_1 (and_1_out, not_1_out, YCOUNT_carry);
  Counter #(.max('h1f), .width(5)) counter_1 (
    .clr(and_1_out), .clk(comparator_3_eq), .carry(counter_1_carry), .Q(S_X));  // open: load, up, count, D
  Counter #(.max('h1f), .trigger("falling"), .width(5)) YCOUNT (
    .clk(counter_1_carry), .carry(YCOUNT_carry), .Q(S_Y));  // open: clr, load, up, count, D

  assign S_CLK = CPU_CLK;
  assign S_DATA = {R, G, B};
endmodule
