// Logisim project comparator.circ as structural Verilog: 3 circuits, main circuit comparator
module comparator (
  input  a,
  input  b,
  input  c,
  input  d,
  output x,
  output y
);

  wire and_1_out, and_2_out, and_3_out, and_4_out, and_5_out, not_1_out, not_2_out, not_3_out, not_4_out,
       not_5_out;

  not not_1 (not_1_out, b);
  and and_1 (and_1_out, not_1_out, c);
  and and_2 (and_2_out, a, not_2_out);
  not not_2 (not_2_out, b);
  and and_3 (and_3_out, a, c);
  not not_3 (not_3_out, a);
  not not_4 (not_4_out, b);
  not not_5 (not_5_out, c);
  or or_1 (x, and_1_out, and_2_out, and_3_out);
  and and_4 (and_4_out, not_3_out, not_4_out, not_5_out, d);
  or or_2 (y, and_4_out, and_5_out);
  and and_5 (and_5_out, a, b, d);
endmodule

module _8_bit_comparator (
  input  in_1,
  input  in_2,
  input  [7:0] in_3,
  input  [7:0] in_4,
  output out_5,
  output out_6
);

  wire comparator_1_x, comparator_1_y, comparator_2_x, comparator_2_y, comparator_3_x, comparator_3_y,
       comparator_4_x, comparator_4_y, comparator_5_x, comparator_5_y, comparator_6_x, comparator_6_y,
       comparator_7_x, comparator_7_y;

  comparator comparator_1 (
    .a(in_3[1]), .b(in_4[1]), .x(comparator_1_x), .c(comparator_2_x), .d(comparator_2_y), .y(comparator_1_y));
  comparator comparator_2 (.a(in_3[0]), .b(in_4[0]), .x(comparator_2_x), .c(in_1), .d(in_2), .y(comparator_2_y));
  comparator comparator_3 (
    .a(in_3[2]), .b(in_4[2]), .x(comparator_3_x), .c(comparator_1_x), .d(comparator_1_y), .y(comparator_3_y));
  comparator comparator_4 (
    .a(in_3[3]), .b(in_4[3]), .x(comparator_4_x), .c(comparator_3_x), .d(comparator_3_y), .y(comparator_4_y));
  comparator comparator_5 (
    .a(in_3[6]), .b(in_4[6]), .x(comparator_5_x), .c(comparator_6_x), .d(comparator_6_y), .y(comparator_5_y));
  comparator comparator_6 (
    .a(in_3[5]), .b(in_4[5]), .x(comparator_6_x), .c(comparator_7_x), .d(comparator_7_y), .y(comparator_6_y));
  comparator comparator_7 (
    .a(in_3[4]), .b(in_4[4]), .x(comparator_7_x), .c(comparator_4_x), .d(comparator_4_y), .y(comparator_7_y));
  comparator comparator_8 (.a(in_3[7]), .b(in_4[7]), .x(out_5), .c(comparator_5_x), .d(comparator_5_y), .y(out_6));
endmodule

module _16_bit_comparator (
  input  in_1,
  input  in_2,
  input  [15:0] in_3,
  input  [15:0] in_4,
  output out_5,
  output out_6
);

  wire n8_bit_comparator_2_out_5, n8_bit_comparator_2_out_6;

  _8_bit_comparator u_8_bit_comparator_1 (
    .in_1(n8_bit_comparator_2_out_5), .in_2(n8_bit_comparator_2_out_6), .in_3(in_3[15:8]), .in_4(in_4[15:8]),
    .out_6(out_6), .out_5(out_5));
  _8_bit_comparator u_8_bit_comparator_2 (
    .in_1(in_1), .in_2(in_2), .in_3(in_3[7:0]), .in_4(in_4[7:0]), .out_6(n8_bit_comparator_2_out_6),
    .out_5(n8_bit_comparator_2_out_5));
endmodule
