// Logisim project flipflops.circ as structural Verilog: 7 circuits, main circuit Risky_D_flip_flop_d9f43a4e
module Risky_D_flip_flop_d9f43a4e (
  input  in_1,
  input  in_2
);

  wire multiplexer_1_out;

  Multiplexer #(.enable("false")) multiplexer_1 (
    .in0(multiplexer_1_out), .in1(in_1), .out(multiplexer_1_out), .sel(in_2));
endmodule

module RS_flip_flop_f71ed703 (
  input  in_1,
  input  in_2,
  output out_3,
  output out_4
);

  wire not_1_out, not_2_out;

  not not_1 (not_1_out, in_1);
  not not_2 (not_2_out, in_2);
  nand nand_1 (out_3, not_1_out, out_4);
  nand nand_2 (out_4, out_3, not_2_out);

  // Notes on the sheet:
  //   out_4: pull=down
  //   out_3: pull=down
endmodule

module D_flipflop_using_RS_755195ad (
  input  in_1,
  input  b,
  output out_3,
  output out_4
);

  wire nand_1_out, nand_2_out;

  nand nand_1 (nand_1_out, in_1, b);
  nand nand_2 (nand_2_out, nand_1_out, b);
  nand nand_3 (out_3, nand_1_out, out_4);
  nand nand_4 (out_4, out_3, nand_2_out);
endmodule

module Clocked_rs_flip_flop_0429bd20 (
  input  S,
  input  CLK,
  input  R,
  output out_4,
  output out_5
);

  wire and_1_out, and_2_out;

  and and_1 (and_1_out, S, CLK);
  and and_2 (and_2_out, CLK, R);
  RS_flip_flop_f71ed703 rs_flip_flop_f71ed703_1 (.in_1(and_1_out), .in_2(and_2_out), .out_3(out_4), .out_4(out_5));
endmodule

module JK_flip_broken_26cfc8b0 (
  input  in_1,
  input  in_2,
  input  in_3
);

  wire and_1_out, and_2_out, rs_flip_flop_f71ed703_1_out_3, rs_flip_flop_f71ed703_1_out_4;

  and and_1 (and_1_out, rs_flip_flop_f71ed703_1_out_3, in_1, in_2);
  RS_flip_flop_f71ed703 rs_flip_flop_f71ed703_1 (
    .in_1(and_1_out), .in_2(and_2_out), .out_3(rs_flip_flop_f71ed703_1_out_3),
    .out_4(rs_flip_flop_f71ed703_1_out_4));
  and and_2 (and_2_out, in_2, in_3, rs_flip_flop_f71ed703_1_out_4);
endmodule

module D_flip_flop_master_slave_1fd38fc7 (
  input  D,
  input  CLK,
  output out_3,
  output out_4
);

  wire d_flipflop_using_rs_755195ad_1_out_3, not_1_out;

  D_flipflop_using_RS_755195ad d_flipflop_using_rs_755195ad_1 (
    .in_1(D), .b(CLK), .out_3(d_flipflop_using_rs_755195ad_1_out_3));  // open: out_4
  not not_1 (not_1_out, CLK);
  D_flipflop_using_RS_755195ad d_flipflop_using_rs_755195ad_2 (
    .in_1(d_flipflop_using_rs_755195ad_1_out_3), .b(not_1_out), .out_3(out_3), .out_4(out_4));
endmodule

module DEMOS (
  input  in_1,
  output out_2,
  output out_3
);

  wire clock_1_out;

  D_flip_flop_master_slave_1fd38fc7 d_flip_flop_master_slave_1fd38fc7_1 (
    .D(in_1), .CLK(clock_1_out), .out_3(out_2), .out_4(out_3));
  Clock clock_1 (.out(clock_1_out));
endmodule
