// Logisim project fulladder.circ as structural Verilog: 5 circuits, main circuit Full_adder_8e202356
module Full_adder_8e202356 (
  input  x,
  input  y,
  input  C,
  output out_4,
  output out_5
);

  wire and_1_out, and_2_out, or_1_out;

  xor xor_1 (out_4, C, y, x);
  and and_1 (and_1_out, y, x);
  or or_1 (or_1_out, x, y);
  and and_2 (and_2_out, C, or_1_out);
  or or_2 (out_5, and_1_out, and_2_out);
endmodule

module Half_adder_af4983ac (
  input  a,
  input  b,
  output x,
  output y
);

  xor xor_1 (x, a, b);
  and and_1 (y, a, b);
endmodule

module L_4_bit_adder_97d5ecdd (
  input  [3:0] in_1,
  input  [3:0] in_2,
  output [4:0] out_3
);

  wire full_adder_8e202356_1_out_5, full_adder_8e202356_2_out_5, full_adder_8e202356_3_out_5;

  Full_adder_8e202356 full_adder_8e202356_1 (
    .out_5(full_adder_8e202356_1_out_5), .out_4(out_3[0]), .C(1'b0), .x(in_1[0]), .y(in_2[0]));
  Full_adder_8e202356 full_adder_8e202356_2 (
    .out_5(full_adder_8e202356_2_out_5), .out_4(out_3[1]), .C(full_adder_8e202356_1_out_5), .x(in_1[1]),
    .y(in_2[1]));
  Full_adder_8e202356 full_adder_8e202356_3 (
    .out_5(full_adder_8e202356_3_out_5), .out_4(out_3[2]), .C(full_adder_8e202356_2_out_5), .x(in_1[2]),
    .y(in_2[2]));
  Full_adder_8e202356 full_adder_8e202356_4 (
    .out_5(out_3[4]), .out_4(out_3[3]), .C(full_adder_8e202356_3_out_5), .x(in_1[3]), .y(in_2[3]));
endmodule

module L_8_bit_adder_56e5dae9 (
  input  [7:0] in_1,
  input  [7:0] in_2,
  output [8:0] out_3
);

  wire full_adder_2_e208ef4c_1_u, full_adder_2_e208ef4c_2_u, full_adder_2_e208ef4c_3_u,
       full_adder_2_e208ef4c_4_u, full_adder_2_e208ef4c_5_u, full_adder_2_e208ef4c_6_u,
       full_adder_2_e208ef4c_7_u;

  Full_adder_2_e208ef4c full_adder_2_e208ef4c_1 (
    .z(out_3[0]), .u(full_adder_2_e208ef4c_1_u), .C(1'b0), .x(in_2[0]), .y(in_1[0]));
  Full_adder_2_e208ef4c full_adder_2_e208ef4c_2 (
    .z(out_3[1]), .u(full_adder_2_e208ef4c_2_u), .C(full_adder_2_e208ef4c_1_u), .x(in_2[1]), .y(in_1[1]));
  Full_adder_2_e208ef4c full_adder_2_e208ef4c_3 (
    .z(out_3[2]), .u(full_adder_2_e208ef4c_3_u), .C(full_adder_2_e208ef4c_2_u), .x(in_2[2]), .y(in_1[2]));
  Full_adder_2_e208ef4c full_adder_2_e208ef4c_4 (
    .z(out_3[3]), .u(full_adder_2_e208ef4c_4_u), .C(full_adder_2_e208ef4c_3_u), .x(in_2[3]), .y(in_1[3]));
  Full_adder_2_e208ef4c full_adder_2_e208ef4c_5 (
    .z(out_3[4]), .u(full_adder_2_e208ef4c_5_u), .C(full_adder_2_e208ef4c_4_u), .x(in_2[4]), .y(in_1[4]));
  Full_adder_2_e208ef4c full_adder_2_e208ef4c_6 (
    .z(out_3[5]), .u(full_adder_2_e208ef4c_6_u), .C(full_adder_2_e208ef4c_5_u), .x(in_2[5]), .y(in_1[5]));
  Full_adder_2_e208ef4c full_adder_2_e208ef4c_7 (
    .z(out_3[6]), .u(full_adder_2_e208ef4c_7_u), .C(full_adder_2_e208ef4c_6_u), .x(in_2[6]), .y(in_1[6]));
  Full_adder_2_e208ef4c full_adder_2_e208ef4c_8 (
    .z(out_3[7]), .u(out_3[8]), .C(full_adder_2_e208ef4c_7_u), .x(in_2[7]), .y(in_1[7]));
endmodule

module Full_adder_2_e208ef4c (
  input  x,
  input  y,
  input  C,
  output z,
  output u
);

  wire and_1_out, and_2_out, and_3_out, and_4_out, and_5_out, and_6_out, and_7_out, not_1_out, not_2_out,
       not_3_out, not_4_out, not_5_out, not_6_out;

  not not_1 (not_1_out, x);
  not not_2 (not_2_out, y);
  not not_3 (not_3_out, x);
  not not_4 (not_4_out, C);
  not not_5 (not_5_out, y);
  not not_6 (not_6_out, C);
  and and_1 (and_1_out, y, C);
  and and_2 (and_2_out, x, C);
  and and_3 (and_3_out, x, y);
  and and_4 (and_4_out, not_1_out, not_2_out, C);
  and and_5 (and_5_out, not_3_out, y, not_4_out);
  and and_6 (and_6_out, x, not_5_out, not_6_out);
  and and_7 (and_7_out, x, y, C);
  or or_1 (u, and_1_out, and_2_out, and_3_out);
  or or_2 (z, and_4_out, and_5_out, and_6_out, and_7_out);
endmodule
