// Logisim project halfadder.circ as structural Verilog: 1 circuit, main circuit Half adder
module Half_adder (
  input  a,
  input  b,
  output x,
  output y
);

  xor xor_1 (x, a, b);
  and and_1 (y, a, b);
endmodule
