// Logisim project screentest.circ as structural Verilog: 2 circuits, main circuit main
module main (
);

  wire clock_1_out, counter_1_carry, counter_3_carry, counter_4_carry, decoder_1_out0, decoder_1_out1,
       decoder_1_out2, decoder_1_out3, delay_1_out_3;
  wire [1:0] counter_1_q;
  wire [4:0] counter_3_q, counter_4_q;
  wire [7:0] register_1_q, register_2_q, register_3_q, rom_1_data;
  wire [11:0] counter_2_q;

  Clock clock_1 (.out(clock_1_out));
  Counter #(.max('h3), .width(2)) counter_1 (
    .clk(clock_1_out), .carry(counter_1_carry), .Q(counter_1_q));  // open: clr, load, up, count, D
  Counter #(.max('h3ff), .width(12)) counter_2 (
    .clk(decoder_1_out3), .Q(counter_2_q));  // open: clr, load, up, count, D, carry
  Decoder #(.enable("false"), .select(2)) decoder_1 (
    .out0(decoder_1_out0), .out1(decoder_1_out1), .out2(decoder_1_out2), .out3(decoder_1_out3),
    .sel(counter_1_q));
  delay delay_1 (.out_3(delay_1_out_3), .X(decoder_1_out3), .CLK(clock_1_out));
  ROM #(.addrWidth(12)) rom_1 (.addr(counter_2_q), .data(rom_1_data));
  Counter #(.max('h1f), .width(5)) counter_3 (
    .clk(delay_1_out_3), .carry(counter_3_carry), .Q(counter_3_q));  // open: clr, load, up, count, D
  Register register_1 (.D(rom_1_data), .en(decoder_1_out0), .clk(clock_1_out), .Q(register_1_q));  // open: clr
  Register register_2 (.D(rom_1_data), .en(decoder_1_out1), .clk(clock_1_out), .Q(register_2_q));  // open: clr
  Register register_3 (.D(rom_1_data), .en(decoder_1_out2), .clk(clock_1_out), .Q(register_3_q));  // open: clr
  Counter #(.max('h1f), .trigger("falling"), .width(5)) counter_4 (
    .clk(counter_3_carry), .carry(counter_4_carry), .Q(counter_4_q));  // open: clr, load, up, count, D
  // RGB_Video #(.height(32), .scale(5), .width(32)) rgb_video_1: pin names not known; wires that end beside it: decoder_1_out0, rom_1_data, counter_4_carry, clock_1_out, counter_1_carry, counter_3_q, counter_4_q, {register_3_q, register_2_q, register_1_q}, clock_1_out

  // Notes on the sheet:
  //   contents of rom_1 (hex, n*v repeats v):
  //   ff ff ff 0 0 0 ff ff ff
endmodule

module delay (
  input  X,
  input  CLK,
  output out_3
);

  wire d_ff_1_q, not_1_out;

  D_Flip_Flop d_ff_1 (.D(X), .clk(not_1_out), .Q(d_ff_1_q));  // open: Qn, preset, reset
  not not_1 (not_1_out, CLK);
  D_Flip_Flop d_ff_2 (.D(d_ff_1_q), .clk(CLK), .Q(out_3));  // open: Qn, preset, reset
endmodule
